# Fritzing sketch car (saved by Fritzing 0.9.2b)

parts:
  Part1 = Arduino Uno (Rev3)
  J1 = Basic Servo
  M1 = DC Motor
  S1 = H-Bridge with L298N
  Part2 = SRF05 Ultrasonic Rangefinder
  VCC1 = Battery block 9V  # not connected
  VCC2 = Battery

nets:
  N1: Part1.D9_PWM, J1.pulse
  N2: Part1.D10_PWM/SS, Part2.Trig
  N3: Part1.D11_PWM/MOSI, Part2.Echo
  GND: Part1.GND, J1.gnd, S1.GND, Part2.GND, VCC2.-
  N4: Part1.D2, S1.IN2
  N5: Part1.D4, S1.IN1
  N6: Part1.D5_PWM, S1.ENA
  VCC: Part1.5V, J1.vcc, Part2.VCC
  N7: M1.pin_1, S1.M2-02
  N8: M1.pin_2, S1.M2-01

custom parts:
  H-Bridge with L298N: h-bridge
